# Fritzing sketch button (saved by Fritzing 0.9.2b)
breadboards: 1

parts:
  パーツ1 = CHIRIMEN
  LED1 = LED - 5mm [color="Red (633nm)" package="5 mm [THT]"]
  R1 = Resistor [tolerance=±5% resistance=150 package=THT]

nets:
  N1: パーツ1.CN1-1_GND, LED1.cathode
  N2: パーツ1.CN1-9_SPI0_RX, R1.Pin_0
  N3: LED1.anode, R1.Pin_1

custom parts:
  CHIRIMEN: CHIRIMEN board.
