# Fritzing sketch curcuit (saved by Fritzing 0.9.2b)
breadboards: 1
perfboards: 1

parts:
  パーツ1 = CHIRIMEN
  R1 = Resistor [tolerance=±5% resistance=220 package=THT]
  R2 = Resistor [tolerance=±5% resistance=220 package=THT]

nets:
  N1: パーツ1.CN1-2_I2C2_SDA, R2.Pin_0
  N2: パーツ1.CN1-3_I2C2_SCL, R1.Pin_0
  N3: パーツ1.CN1-16_VCC_3V3, R1.Pin_1, R2.Pin_1

notes:
  GP2Y0E03
  VDD
  Vout
  GND
  VIN
  GPIO1
  SCL
  SDA

custom parts:
  CHIRIMEN: CHIRIMEN board.
