# Fritzing sketch PCA9685 (saved by Fritzing 0.9.2b)

parts:
  パーツ1 = CHIRIMEN
  パーツ2 = 16-Channel 12-bit PCA9685 PWM/Servo Driver
  J1 = Basic Servo

nets:
  VCC: パーツ1.CN2-18_VSYS(5V), パーツ2.V+, パーツ2.VCC, J1.vcc
  GND: パーツ1.CN2-17_GND, パーツ2.GND, J1.gnd
  N1: パーツ1.CN2-11_I2C0_SCL, パーツ2.SCL
  N2: パーツ1.CN2-12_I2C0_SDA, パーツ2.SDA
  N3: パーツ2.0, J1.pulse

custom parts:
  CHIRIMEN: CHIRIMEN board.
  16-Channel 12-bit PCA9685 PWM/Servo Driver: The Adafruit 16-Channel 12-bit PWM/Servo Driver will drive up to 16 servos over I2C with only 2 pins. The on-board PCA9685 PWM controller will drive all 16 channels simultaneously with no additional processing overhead. What's more, you can chain up to 62 of them to control up to 992 servos - all with the same 2 pins
