# Fritzing sketch grove-accelerometer (saved by Fritzing 0.9.2b)

parts:
  パーツ1 = CHIRIMEN
  Grove1 = Grove 3 Axis Digital Accelerometer 16g

nets:
  N1: パーツ1.CN2-18_VSYS(5V), Grove1.VCC
  N2: パーツ1.CN2-17_GND, Grove1.GND
  N3: パーツ1.CN2-11_I2C0_SCL, Grove1.SCL
  N4: パーツ1.CN2-12_I2C0_SDA, Grove1.SDA

custom parts:
  CHIRIMEN: CHIRIMEN board.
